# Fritzing sketch Day_02_Light_LED (saved by Fritzing 1.0.0rc)
breadboards: 1

parts:
  Part1 = Arduino Mega 2560 (Rev3)
  LED1 = LEDs [package=led10mm]
  R1 = Resistor [tolerance=±5% power=0.25W resistance=100 package=THT]

nets:
  N1: Part1.GND, LED1.A
  N2: Part1.D22, R1.Pin_1
  N3: LED1.C, R1.Pin_0
