# Fritzing sketch Day_03_Light_With_Switch (saved by Fritzing 1.0.0rc)
breadboards: 1

parts:
  Part1 = Arduino Mega 2560 (Rev3)
  LED1 = LEDs [package=led10mm]
  R1 = Resistor [tolerance=±5% power=0.25W resistance=100 package=THT]
  S1 = Pushbutton [package="[SMD]"]
  R2 = Resistor [tolerance=±5% power=0.25W resistance=100 package=THT]

nets:
  N1: Part1.GND, LED1.A, R2.Pin_0
  N2: Part1.5V, S1.Pin_3, S1.Pin_4
  N3: Part1.D22, R1.Pin_1
  N4: Part1.D24, S1.Pin_1, S1.Pin_2, R2.Pin_1
  N5: LED1.C, R1.Pin_0
