# Fritzing sketch Day_07 Motion Sensor (saved by Fritzing 1.0.0rc)
breadboards: 3

parts:
  Part1 = Arduino Mega 2560 (Rev3)
  interiorLightsButton = Pushbutton [package="[SMD]"]
  batteryStatusLight = smd LED [color="Red (633nm)" package="1206 [SMD]"]
  R3 = Resistor [tolerance=±5% power=0.25W resistance=220 package=THT]
  R4 = Resistor [tolerance=±5% power=0.25W resistance=220 package=THT]
  solarArray = PHOTOCELL [package=photocell-kit]
  R6 = Resistor [tolerance=±5% power=0.25W resistance=200 package=THT]
  R7 = Resistor [tolerance=±5% power=0.25W resistance=220 package=THT]
  interiorLighting = smd LED [color="White (4500K)" package="0603 [SMD]"]
  alarmSystem = Passive Buzzer
  Exterior_Light_Override = Pushbutton [package="[SMD]"]
  Alarm_Override = Pushbutton [package="[SMD]"]
  Exterior_Floodlights = smd LED [color="White (4500K)" package="0603 [SMD]"]
  Exterior_Alert = smd LED [color="Red (633nm)" package="1206 [SMD]"]
  R8 = Resistor [tolerance=±5% power=0.25W resistance=220 package=THT]
  R9 = Resistor [tolerance=±5% power=0.25W resistance=220 package=THT]
  PIR_Sensor = HC-SR501 Body Sensor Module

nets:
  GND: Part1.GND, R7.Pin_0, interiorLighting.cathode, alarmSystem.-, Exterior_Floodlights.cathode, Exterior_Alert.cathode, PIR_Sensor.GND
  N1: Part1.D13_PWM, alarmSystem.S
  N2: Part1.D12_PWM, R6.Pin_1
  5V: Part1.5V, interiorLightsButton.Pin_3, interiorLightsButton.Pin_4, solarArray.P$2, Exterior_Light_Override.Pin_3, Exterior_Light_Override.Pin_4, Alarm_Override.Pin_3, Alarm_Override.Pin_4, PIR_Sensor.VCC
  N3: Part1.D22, solarArray.P$1, R7.Pin_1
  N4: Part1.D24, interiorLightsButton.Pin_1, interiorLightsButton.Pin_2
  N5: Part1.D26, R3.Pin_1
  N6: Part1.D27, R4.Pin_1
  N7: Part1.D28, PIR_Sensor.OUT
  N8: Part1.D29, Exterior_Light_Override.Pin_1, Exterior_Light_Override.Pin_2
  N9: Part1.D31, Alarm_Override.Pin_1, Alarm_Override.Pin_2
  N10: Part1.D32, R9.Pin_1
  N11: Part1.D33, R8.Pin_1
  N12: batteryStatusLight.cathode, R4.Pin_0
  N13: batteryStatusLight.anode, R3.Pin_0
  N14: R6.Pin_0, interiorLighting.anode
  N15: Exterior_Floodlights.anode, R8.Pin_0
  N16: Exterior_Alert.anode, R9.Pin_0

custom parts:
  HC-SR501 Body Sensor Module: Pyroelectric Infrared PIR Motion Sensor Detector Module
